# Fritzing sketch Exp06_LunchBox_HelloSwitch_PullDown (saved by Fritzing 0.9.3b)
breadboards: 1

parts:
  Part1 = DIP - 18 pins
  S2 = Pushbutton [package="[SMD]"]

nets:
  N1: Part1.3V3, Part1.P1.4, S2.Pin_3, S2.Pin_4
  N2: S2.Pin_1, S2.Pin_2
