# Fritzing sketch Exp07_LunchBox_HelloSwitch_PullUp (saved by Fritzing 0.9.3b)
breadboards: 1

parts:
  Part1 = DIP - 18 pins
  S2 = Pushbutton [package="[SMD]"]

nets:
  N1: Part1.P1.4, Part1.GND, S2.Pin_3, S2.Pin_4
  N2: S2.Pin_1, S2.Pin_2
