# Fritzing sketch Exp09_LunchBox_HelloResetSource (saved by Fritzing 0.9.3b)
breadboards: 1

parts:
  Part1 = DIP - 18 pins
  LED1 = LEDs [package=led10mm]
  R1 = Resistor [tolerance=±5% resistance=220 package="0603 [SMD]"]
  LED2 = LEDs [package=led10mm]
  R2 = Resistor [tolerance=±5% resistance=220 package="0603 [SMD]"]
  LED3 = LEDs [package=led10mm]
  R3 = Resistor [tolerance=±5% resistance=220 package="0603 [SMD]"]
  LED4 = LEDs [package=led10mm]
  R4 = Resistor [tolerance=±5% resistance=220 package="0603 [SMD]"]

nets:
  N1: Part1.P1.0, R1.Pin_1
  N2: Part1.P1.1, R2.Pin_1
  N3: Part1.P1.2, R3.Pin_1
  N4: Part1.P1.3, R4.Pin_1
  N5: Part1.GND, LED1.C, LED2.C, LED3.C, LED4.C
  N6: LED1.A, R1.Pin_0
  N7: LED2.A, R2.Pin_0
  N8: LED3.A, R3.Pin_0
  N9: LED4.A, R4.Pin_0
